// Logisim project e2380103.circ as structural Verilog: 1 circuit, main circuit main
module main (
  input  O1,
  input  O0,
  input  S,
  input  A1,
  input  A0,
  input  B1,
  input  B0,
  output E,
  output G,
  output B,
  output L,
  output L0,
  output L1,
  output L2,
  output L3,
  output L4,
  output L5,
  output L6,
  output L7,
  output N
);

  wire and_1_out, and_2_out, and_3_out, and_4_out, and_5_out, n3_to_8_decoder_74138_1_p4,
       n3_to_8_decoder_74138_1_p5, n3_to_8_decoder_74138_1_p6, n3_to_8_decoder_74138_1_p7,
       n3_to_8_decoder_74138_1_p8, n3_to_8_decoder_74138_1_p9, n3_to_8_decoder_74138_1_p10,
       n3_to_8_decoder_74138_2_p7, n3_to_8_decoder_74138_2_p8, n3_to_8_decoder_74138_2_p9,
       n3_to_8_decoder_74138_2_p10, n3_to_8_decoder_74138_2_p11, n3_to_8_decoder_74138_2_p12,
       n3_to_8_decoder_74138_2_p13, n3_to_8_decoder_74138_2_p14, n3_to_8_decoder_74138_3_p9,
       n3_to_8_decoder_74138_3_p10, n3_to_8_decoder_74138_3_p11, n3_to_8_decoder_74138_3_p12,
       n3_to_8_decoder_74138_3_p13, n3_to_8_decoder_74138_3_p14, n3_to_8_decoder_74138_4_p4,
       n3_to_8_decoder_74138_4_p5, n3_to_8_decoder_74138_4_p6, n3_to_8_decoder_74138_4_p7,
       n3_to_8_decoder_74138_5_p7, n3_to_8_decoder_74138_5_p8, n3_to_8_decoder_74138_5_p9,
       n3_to_8_decoder_74138_5_p10, n3_to_8_decoder_74138_5_p11, n3_to_8_decoder_74138_5_p12,
       n3_to_8_decoder_74138_5_p13, n3_to_8_decoder_74138_6_p7, n3_to_8_decoder_74138_6_p8,
       n3_to_8_decoder_74138_6_p9, n3_to_8_decoder_74138_6_p10, n3_to_8_decoder_74138_6_p11,
       n3_to_8_decoder_74138_6_p12, n3_to_8_decoder_74138_6_p13, n3_to_8_decoder_74138_6_p14,
       n3_to_8_decoder_74138_6_p15, n3_to_8_decoder_74138_7_p7, n3_to_8_decoder_74138_7_p8,
       n3_to_8_decoder_74138_7_p9, n3_to_8_decoder_74138_7_p10, n3_to_8_decoder_74138_7_p11,
       n3_to_8_decoder_74138_7_p12, n3_to_8_decoder_74138_7_p13, n3_to_8_decoder_74138_8_p10,
       n3_to_8_decoder_74138_8_p11, n3_to_8_decoder_74138_8_p12, n3_to_8_decoder_74138_8_p13,
       n3_to_8_decoder_74138_8_p14, n3_to_8_decoder_74138_8_p15, n3_to_8_decoder_74138_8_p16,
       n3_to_8_decoder_74138_8_p17, n3_to_8_decoder_74138_8_p18, not_1_out, not_2_out, not_3_out, not_4_out,
       not_5_out, not_6_out, not_8_out, not_9_out, not_10_out, not_11_out, not_12_out, not_13_out,
       not_14_out, not_15_out, not_16_out, not_17_out, not_18_out, not_19_out, not_20_out, not_21_out,
       not_22_out, not_23_out, not_24_out, not_25_out, not_26_out, not_27_out, not_28_out, not_29_out,
       not_30_out, not_31_out, not_32_out, not_33_out, not_34_out, not_35_out, not_36_out, not_37_out,
       not_38_out, not_39_out, not_40_out, not_41_out, not_42_out, not_43_out, not_44_out, not_45_out,
       not_46_out, not_47_out, not_48_out, not_49_out, not_50_out, not_51_out, not_52_out, not_53_out,
       not_54_out, not_55_out, not_56_out, not_57_out, not_58_out, not_59_out, not_60_out, not_61_out,
       not_62_out, not_63_out, or_1_out, or_3_out, or_4_out, or_5_out, or_6_out, or_7_out, or_8_out,
       or_9_out, or_10_out, or_11_out, or_12_out, or_13_out, or_14_out, or_15_out, or_16_out, or_17_out,
       or_18_out, or_19_out, or_20_out, or_21_out, or_22_out, or_23_out, or_24_out, or_25_out, or_26_out,
       or_27_out, or_29_out, or_30_out, or_31_out, or_32_out, or_33_out, or_34_out, or_35_out, or_36_out,
       or_37_out, or_38_out, or_39_out, or_41_out, or_42_out, or_44_out;

  not not_1 (not_1_out, S);
  not not_2 (not_2_out, O0);
  not not_3 (not_3_out, S);
  not not_4 (not_4_out, and_1_out);
  and and_1 (and_1_out, O1, O0);
  and and_2 (and_2_out, O1, not_2_out);
  not not_5 (not_5_out, A1);
  and and_3 (and_3_out, and_2_out, not_3_out);
  and and_4 (and_4_out, A1, and_3_out);
  not not_6 (not_6_out, and_4_out);
  // _3_to_8_decoder__74138 #(.Facing("east")) 3_to_8_decoder_74138_1: pin names not known; wires that end beside it: B0, B1, A0, n3_to_8_decoder_74138_1_p4, n3_to_8_decoder_74138_1_p5, n3_to_8_decoder_74138_1_p6, n3_to_8_decoder_74138_1_p7, n3_to_8_decoder_74138_1_p8, n3_to_8_decoder_74138_1_p9, n3_to_8_decoder_74138_1_p10
  // _3_to_8_decoder__74138 #(.Facing("east")) 3_to_8_decoder_74138_2: pin names not known; wires that end beside it: B0, B1, A0, not_5_out, O1, O0, n3_to_8_decoder_74138_2_p7, n3_to_8_decoder_74138_2_p8, n3_to_8_decoder_74138_2_p9, n3_to_8_decoder_74138_2_p10, n3_to_8_decoder_74138_2_p11, n3_to_8_decoder_74138_2_p12, n3_to_8_decoder_74138_2_p13, n3_to_8_decoder_74138_2_p14
  // _3_to_8_decoder__74138 #(.Facing("east")) 3_to_8_decoder_74138_3: pin names not known; wires that end beside it: A0, A1, B0, A1, O0, O1, O1, O0, n3_to_8_decoder_74138_3_p9, n3_to_8_decoder_74138_3_p10, n3_to_8_decoder_74138_3_p11, n3_to_8_decoder_74138_3_p12, n3_to_8_decoder_74138_3_p13, n3_to_8_decoder_74138_3_p14
  not not_7 (n3_to_8_decoder_74138_3_p9, 1'b1);
  and and_5 (and_5_out, not_6_out, and_3_out);
  // _3_to_8_decoder__74138 #(.Facing("east")) 3_to_8_decoder_74138_4: pin names not known; wires that end beside it: A0, A1, n3_to_8_decoder_74138_3_p9, n3_to_8_decoder_74138_4_p4, n3_to_8_decoder_74138_4_p5, n3_to_8_decoder_74138_4_p6, n3_to_8_decoder_74138_4_p7
  // _3_to_8_decoder__74138 #(.Facing("east")) 3_to_8_decoder_74138_5: pin names not known; wires that end beside it: B0, B1, A0, O1, O0, not_3_out, n3_to_8_decoder_74138_5_p7, n3_to_8_decoder_74138_5_p8, n3_to_8_decoder_74138_5_p9, n3_to_8_decoder_74138_5_p10, n3_to_8_decoder_74138_5_p11, n3_to_8_decoder_74138_5_p12, n3_to_8_decoder_74138_5_p13
  // _3_to_8_decoder__74138 #(.Facing("east")) 3_to_8_decoder_74138_6: pin names not known; wires that end beside it: B0, B1, A0, not_5_out, not_4_out, S, n3_to_8_decoder_74138_6_p7, n3_to_8_decoder_74138_6_p8, n3_to_8_decoder_74138_6_p9, n3_to_8_decoder_74138_6_p10, n3_to_8_decoder_74138_6_p11, n3_to_8_decoder_74138_6_p12, n3_to_8_decoder_74138_6_p13, n3_to_8_decoder_74138_6_p14, n3_to_8_decoder_74138_6_p15
  // _3_to_8_decoder__74138 #(.Facing("east")) 3_to_8_decoder_74138_7: pin names not known; wires that end beside it: B0, B1, A0, A1, not_4_out, S, n3_to_8_decoder_74138_7_p7, n3_to_8_decoder_74138_7_p8, n3_to_8_decoder_74138_7_p9, n3_to_8_decoder_74138_7_p10, n3_to_8_decoder_74138_7_p11, n3_to_8_decoder_74138_7_p12, n3_to_8_decoder_74138_7_p13
  // _3_to_8_decoder__74138 #(.Facing("east")) 3_to_8_decoder_74138_8: pin names not known; wires that end beside it: B0, B1, A0, not_5_out, A1, not_4_out, not_4_out, not_1_out, not_1_out, n3_to_8_decoder_74138_8_p10, n3_to_8_decoder_74138_8_p11, n3_to_8_decoder_74138_8_p12, n3_to_8_decoder_74138_8_p13, n3_to_8_decoder_74138_8_p14, n3_to_8_decoder_74138_8_p15, n3_to_8_decoder_74138_8_p16, n3_to_8_decoder_74138_8_p17, n3_to_8_decoder_74138_8_p18
  not not_8 (not_8_out, n3_to_8_decoder_74138_1_p4);
  not not_9 (not_9_out, n3_to_8_decoder_74138_5_p7);
  not not_10 (not_10_out, n3_to_8_decoder_74138_7_p7);
  not not_11 (not_11_out, n3_to_8_decoder_74138_1_p5);
  not not_12 (not_12_out, n3_to_8_decoder_74138_1_p6);
  not not_13 (not_13_out, n3_to_8_decoder_74138_1_p7);
  not not_14 (not_14_out, n3_to_8_decoder_74138_1_p8);
  not not_15 (not_15_out, n3_to_8_decoder_74138_1_p9);
  not not_16 (not_16_out, n3_to_8_decoder_74138_1_p10);
  not not_17 (not_17_out, n3_to_8_decoder_74138_2_p7);
  not not_18 (not_18_out, n3_to_8_decoder_74138_2_p8);
  not not_19 (not_19_out, n3_to_8_decoder_74138_3_p11);
  not not_20 (not_20_out, n3_to_8_decoder_74138_3_p12);
  not not_21 (not_21_out, n3_to_8_decoder_74138_3_p13);
  not not_22 (not_22_out, n3_to_8_decoder_74138_3_p14);
  not not_23 (not_23_out, n3_to_8_decoder_74138_4_p4);
  not not_24 (not_24_out, n3_to_8_decoder_74138_4_p5);
  not not_25 (not_25_out, n3_to_8_decoder_74138_4_p6);
  not not_26 (not_26_out, n3_to_8_decoder_74138_4_p7);
  not not_27 (not_27_out, n3_to_8_decoder_74138_5_p8);
  not not_28 (not_28_out, n3_to_8_decoder_74138_5_p9);
  not not_29 (not_29_out, n3_to_8_decoder_74138_5_p10);
  not not_30 (not_30_out, n3_to_8_decoder_74138_5_p11);
  not not_31 (not_31_out, n3_to_8_decoder_74138_5_p12);
  not not_32 (not_32_out, n3_to_8_decoder_74138_5_p13);
  not not_33 (not_33_out, n3_to_8_decoder_74138_6_p7);
  not not_34 (not_34_out, n3_to_8_decoder_74138_6_p8);
  not not_35 (not_35_out, n3_to_8_decoder_74138_7_p8);
  not not_36 (not_36_out, n3_to_8_decoder_74138_7_p9);
  not not_37 (not_37_out, n3_to_8_decoder_74138_7_p10);
  not not_38 (not_38_out, n3_to_8_decoder_74138_7_p11);
  not not_39 (not_39_out, n3_to_8_decoder_74138_7_p12);
  not not_40 (not_40_out, n3_to_8_decoder_74138_7_p13);
  not not_41 (not_41_out, n3_to_8_decoder_74138_8_p10);
  not not_42 (not_42_out, n3_to_8_decoder_74138_8_p11);
  not not_43 (not_43_out, n3_to_8_decoder_74138_2_p9);
  not not_44 (not_44_out, n3_to_8_decoder_74138_2_p10);
  not not_45 (not_45_out, n3_to_8_decoder_74138_2_p11);
  not not_46 (not_46_out, n3_to_8_decoder_74138_2_p12);
  not not_47 (not_47_out, n3_to_8_decoder_74138_2_p13);
  not not_48 (not_48_out, n3_to_8_decoder_74138_2_p14);
  not not_49 (not_49_out, n3_to_8_decoder_74138_3_p10);
  or or_1 (or_1_out, not_19_out, not_20_out);
  or or_2 (B, or_1_out, or_3_out);
  or or_3 (or_3_out, not_21_out, not_22_out);
  not not_50 (not_50_out, n3_to_8_decoder_74138_6_p9);
  not not_51 (not_51_out, n3_to_8_decoder_74138_6_p10);
  not not_52 (not_52_out, n3_to_8_decoder_74138_6_p11);
  not not_53 (not_53_out, n3_to_8_decoder_74138_6_p12);
  not not_54 (not_54_out, n3_to_8_decoder_74138_6_p13);
  not not_55 (not_55_out, n3_to_8_decoder_74138_6_p14);
  not not_56 (not_56_out, n3_to_8_decoder_74138_6_p15);
  not not_57 (not_57_out, n3_to_8_decoder_74138_8_p12);
  not not_58 (not_58_out, n3_to_8_decoder_74138_8_p13);
  not not_59 (not_59_out, n3_to_8_decoder_74138_8_p14);
  not not_60 (not_60_out, n3_to_8_decoder_74138_8_p15);
  not not_61 (not_61_out, n3_to_8_decoder_74138_8_p16);
  not not_62 (not_62_out, n3_to_8_decoder_74138_8_p17);
  not not_63 (not_63_out, n3_to_8_decoder_74138_8_p18);
  or or_4 (or_4_out, not_29_out, not_32_out);
  or or_5 (or_5_out, or_4_out, or_6_out);
  or or_6 (or_6_out, not_50_out, not_53_out);
  or or_7 (or_7_out, not_61_out, not_42_out);
  or or_8 (or_8_out, not_41_out, not_36_out);
  or or_9 (or_9_out, or_7_out, or_8_out);
  or or_10 (or_10_out, not_31_out, not_28_out);
  or or_11 (or_11_out, or_10_out, not_34_out);
  or or_12 (or_12_out, not_33_out, not_51_out);
  or or_13 (or_13_out, not_62_out, not_59_out);
  or or_14 (or_14_out, not_57_out, not_40_out);
  or or_15 (or_15_out, not_38_out, not_35_out);
  or or_16 (or_16_out, not_35_out, not_36_out);
  or or_17 (or_17_out, not_37_out, not_40_out);
  or or_18 (or_18_out, not_41_out, not_59_out);
  or or_19 (or_19_out, not_27_out, not_30_out);
  or or_20 (or_20_out, or_12_out, not_54_out);
  or or_21 (or_21_out, or_13_out, or_14_out);
  or or_22 (or_22_out, not_10_out, not_39_out);
  or or_23 (or_23_out, not_58_out, not_63_out);
  or or_24 (or_24_out, or_16_out, or_17_out);
  or or_25 (or_25_out, or_21_out, or_15_out);
  or or_26 (or_26_out, not_60_out, not_37_out);
  or or_27 (or_27_out, or_22_out, or_23_out);
  or or_28 (N, or_24_out, or_18_out);
  or or_29 (or_29_out, not_14_out, not_18_out);
  or or_30 (or_30_out, not_43_out, not_48_out);
  or or_31 (or_31_out, not_47_out, not_46_out);
  or or_32 (or_32_out, not_45_out, not_17_out);
  or or_33 (or_33_out, not_16_out, not_13_out);
  or or_34 (or_34_out, not_12_out, not_11_out);
  or or_35 (or_35_out, and_5_out, not_23_out);
  or or_36 (or_36_out, not_9_out, or_27_out);
  or or_37 (or_37_out, and_4_out, or_19_out);
  or or_38 (or_38_out, not_24_out, or_11_out);
  or or_39 (or_39_out, not_8_out, not_15_out);
  or or_40 (E, or_39_out, or_41_out);
  or or_41 (or_41_out, not_44_out, not_49_out);
  or or_42 (or_42_out, or_29_out, or_30_out);
  or or_43 (G, or_42_out, or_31_out);
  or or_44 (or_44_out, or_32_out, or_33_out);
  or or_45 (L, or_44_out, or_34_out);
  or or_46 (L0, or_35_out, or_36_out);
  or or_47 (L1, or_37_out, or_25_out);
  or or_48 (L2, or_38_out, or_9_out);
  or or_49 (L3, or_5_out, or_26_out);
  or or_50 (L4, not_25_out, or_20_out);
  or or_51 (L5, not_52_out, not_55_out);
  or or_52 (L6, not_26_out, not_56_out);
  not not_64 (L7, 1'b1);
endmodule
